// Logisim project Simulation.circ as structural Verilog: 1 circuit, main circuit main
module main (
  input  in_1
);

  wire _1_2, A, and_1_out, and_3_out, and_4_out, and_5_out, AOE, CARRY, CLK, clock_1_out, d_ff_3_qn, IR, JMP,
       n1_2, nCLK, not_1_out, not_2_out, not_3_out, not_4_out, or_5_out, or_6_out, P, PCCLK, READ, ST, SWITCH;
  wire [7:0] adder_1_out, controlled_buffer_2_out, counter_1_q, DATA, multiplexer_1_out, register_1_q,
       register_2_q, register_3_q;

  Register register_1 (.D(DATA), .Q(register_1_q), .clk(P));  // open: en, clr
  Counter counter_1 (
    .load(JMP), .D(register_1_q), .count(not_1_out), .Q(counter_1_q), .clk(PCCLK), .clr(in_1));  // open: carry
  not not_1 (not_1_out, JMP);
  Register register_2 (.D(adder_1_out), .Q(register_2_q), .clk(A));  // open: en, clr
  Adder adder_1 (.a(DATA), .b(register_1_q), .out(adder_1_out), .cin(1'b0), .cout(CARRY));
  Multiplexer #(.width(8)) multiplexer_1 (
    .in0(register_1_q), .in1(counter_1_q), .out(multiplexer_1_out), .sel(SWITCH));  // open: en
  assign DATA = AOE ? register_2_q : 8'bz;  // Controlled_Buffer controlled_buffer_1
  RAM ram_1 (.addr(multiplexer_1_out), .data(DATA), .clk(ST), .ld(READ));  // open: sel, clr
  Pull_Resistor pull_resistor_1 (.node(DATA));
  Register register_3 (.D(DATA), .Q(register_3_q), .clk(IR));  // open: en, clr
  Clock clock_1 (.out(clock_1_out));
  assign {controlled_buffer_2_out[7], SWITCH, controlled_buffer_2_out[5:0]} = _1_2 ? register_3_q : 8'bz;  // Controlled_Buffer controlled_buffer_2
  Pull_Resistor #(.pull(1)) pull_resistor_2 (.node({controlled_buffer_2_out[7], SWITCH, controlled_buffer_2_out[5:0]}));
  D_Flip_Flop d_ff_1 (.Q(CLK), .Qn(nCLK), .preset(clock_1_out), .reset(not_2_out));  // open: clk, D, en
  not not_2 (not_2_out, clock_1_out);
  not not_3 (not_3_out, clock_1_out);
  D_Flip_Flop d_ff_2 (.clk(not_3_out), .D(n1_2), .Q(_1_2), .Qn(n1_2), .reset(in_1));  // open: preset, en
  or or_1 (P, controlled_buffer_2_out[0], and_1_out);
  and and_1 (and_1_out, CLK, _1_2);
  or or_2 (ST, controlled_buffer_2_out[2], and_1_out);
  or or_3 (A, controlled_buffer_2_out[1], and_1_out);
  not not_4 (not_4_out, controlled_buffer_2_out[7]);
  or or_4 (READ, not_4_out, n1_2);
  not not_5 (AOE, controlled_buffer_2_out[5]);
  and and_2 (IR, CLK, n1_2);
  and and_3 (and_3_out, CLK, or_5_out);
  or or_5 (or_5_out, READ, JMP);
  D_Flip_Flop d_ff_3 (.clk(A), .D(CARRY), .Qn(d_ff_3_qn), .reset(in_1));  // open: Q, preset, en
  or or_6 (or_6_out, d_ff_3_qn, controlled_buffer_2_out[4]);
  and and_4 (and_4_out, and_3_out, SWITCH);
  and and_5 (and_5_out, controlled_buffer_2_out[3], or_6_out);
  not not_6 (JMP, and_5_out);
  or or_7 (PCCLK, IR, and_4_out);

  // Other names for the same wires on the sheet: RST = in_1
endmodule
